# Fritzing sketch Esquema de ligação (saved by Fritzing 0.9.3b)
breadboards: 1

parts:
  Componente2 = Arduino Mega ADK (Rev3)
  Componente3 = Arduino Uno (Rev3)
  Componente4 = RFID USB Reader
  R1 = Resistor [tolerance=±5% resistance=220 package=THT]
  R2 = Resistor [tolerance=±5% resistance=220 package=THT]
  LED1 = LED - 5mm [color="Red (633nm)" package="5 mm [THT]"]
  LED2 = LED - 5mm [color="Green (570nm)" package="5 mm [THT]"]
  Componente5 = Arduino Ethernet Shield (Rev3)

nets:
  N1: Componente2.D19/RX1, Componente3.D1/TX
  N2: Componente2.D18/TX1, Componente3.D0/RX
  N3: Componente3.D9_PWM, Componente4.GND
  N4: Componente3.D10_PWM/SS, Componente4.GNDT
  N5: Componente3.D11_PWM/MOSI, Componente4.ANT2
  N6: Componente3.D12/MISO, Componente4.ANT1
  N7: Componente3.D13/SCK, Componente4.CP
  N8: Componente3.GND, Componente4.TX-O
  3V3: Componente3.3V3, Componente4.VCC
  N9: R1.Pin_0, Componente5.PWM_D5
  N10: R1.Pin_1, LED2.cathode, LED2.anode
  N11: R2.Pin_0, Componente5.PWM_D6
  N12: R2.Pin_1, LED1.cathode, LED1.anode, Componente5.GND
